# Fritzing sketch carrito (saved by Fritzing 0.9.0b)
breadboards: 1

parts:
  Parte1 = Arduino Uno (Rev3)
  IC1 = L293D [package=THT]
  U2 = HC-SR04 [chip_label=IC package="SIP (Single Inline) [THT]"]
  BAT1 = BC9VPC [package=bc9vpc]
  M3 = DC Motor
  M2 = DC Motor

nets:
  N1: Parte1.D8, U2.Echo
  N2: Parte1.D9_PWM, IC1.Enable_1
  N3: Parte1.D11_PWM/MOSI, U2.Trig
  N4: Parte1.D2, IC1.In_2
  N5: Parte1.D3_PWM, IC1.In_1
  N6: Parte1.D4, IC1.In_3
  N7: Parte1.D5_PWM, IC1.In_4
  5V: Parte1.5V, IC1.+V, U2.Vcc
  GND: Parte1.GND, U2.GND
  N8: IC1.Out_1_(_Controlled_by_Enable_1_), M3.pin_1
  N9: IC1.Out_2_(_Controlled_by_Enable_1_), M3.pin_2
  N10: IC1.+Vmotor, BAT1.V+
  N11: IC1.Out_3_(_Controlled_by_Enable_2_), M2.pin_2
  N12: IC1.Out_4_(_Controlled_by_Enable_2_), M2.pin_1

custom parts:
  HC-SR04: HC-SR04 ultrasound distance sensor
